# Fritzing sketch arduino-gravity-recorder (saved by Fritzing 0.9.4)

parts:
  Part1 = Arduino Nano (Rev3.0)
  VCC1 = Battery block 9V
  microSD1 = MicroSD Card Module
  Grove1 = Grove 3 Axis Digital Accelerometer 16g
  S1 = Toggle Switch [package=THT]

nets:
  N1: Part1.D10, microSD1.CS
  N2: Part1.D11/MOSI, microSD1.MOSI
  N3: Part1.D12/MISO, microSD1.MISO
  N4: Part1.VIN, S1.COM
  GND: Part1.GND, VCC1.-, microSD1.GND, Grove1.GND
  VCC: Part1.5V, microSD1.VCC, Grove1.VCC
  N5: Part1.A5, Grove1.SCL
  N6: Part1.A4, Grove1.SDA
  N7: Part1.D13/SCK, microSD1.SCK
  N8: VCC1.+, S1.L1

notes:
  Camera Hotshoe
